# Fritzing sketch j5-raspberry-memory-game (saved by Fritzing 0.9.3b)
breadboards: 1

parts:
  Raspberry_Pi_3_Model_B+ = Raspberry Pi 3 [part_number=RPI-3-V1.2]
  Raspberry_PI_GDIO_External_Board = T Cobbler Plus
  BUTTON_ORANGE = Pushbutton [package="[SMD]"]
  LED_ORANGE = LED - 3mm [color="Orange (620nm)" package="3 mm [THT]"]
  R1 = Resistor [tolerance=±5% resistance=10k package=THT]
  LED_GREEN = LED - 3mm [color="Green (555nm)" package="3 mm [THT]"]
  R2 = Resistor [tolerance=±5% resistance=10k package=THT]
  LED_YELLOW = LED - 3mm [color="Yellow (595nm)" package="3 mm [THT]"]
  R3 = Resistor [tolerance=±5% resistance=10k package=THT]
  LED_BLUE = LED - 3mm [color="Blue (430nm)" package="3 mm [THT]"]
  R4 = Resistor [tolerance=±5% resistance=10k package=THT]
  R5 = Resistor [tolerance=±5% resistance=10k package=THT]
  BUTTON_YELLOW = Pushbutton [package="[SMD]"]
  R6 = Resistor [tolerance=±5% resistance=10k package=THT]
  BUTTON_GREEN = Pushbutton [package="[SMD]"]
  R7 = Resistor [tolerance=±5% resistance=10k package=THT]
  PIEZO = Piezo Speaker
  LCD2 = LCD screen
  LCM1602_IIC2 = LCM1602 IIC [part_number="LCM1602 IIC" chip_label="LCM1602 IIC" package="DIP (Dual Inline) [THT]"]

nets:
  3V3: Raspberry_Pi_3_Model_B+.3v3, Raspberry_Pi_3_Model_B+.3V3, Raspberry_PI_GDIO_External_Board.3.3V#41, Raspberry_PI_GDIO_External_Board.3.3V#57
  N1: Raspberry_Pi_3_Model_B+.GPIO2, Raspberry_PI_GDIO_External_Board.GPIO_2
  N2: Raspberry_Pi_3_Model_B+.GPIO3, Raspberry_PI_GDIO_External_Board.GPIO_3
  N3: Raspberry_Pi_3_Model_B+.GPIO4, Raspberry_PI_GDIO_External_Board.GPIO_4
  N4: Raspberry_Pi_3_Model_B+.GND, Raspberry_PI_GDIO_External_Board.GND#46, Raspberry_PI_GDIO_External_Board.GND#49, Raspberry_PI_GDIO_External_Board.GND#54, Raspberry_PI_GDIO_External_Board.GND#60, Raspberry_PI_GDIO_External_Board.GND#65, Raspberry_PI_GDIO_External_Board.GND#70, Raspberry_PI_GDIO_External_Board.GND#74, Raspberry_PI_GDIO_External_Board.GND#79
  N5: Raspberry_Pi_3_Model_B+.GPIO17, Raspberry_PI_GDIO_External_Board.GPIO_17
  N6: Raspberry_Pi_3_Model_B+.GPIO27, Raspberry_PI_GDIO_External_Board.GPIO_27
  N7: Raspberry_Pi_3_Model_B+.GPIO22, Raspberry_PI_GDIO_External_Board.GPIO_22
  N8: Raspberry_Pi_3_Model_B+.GPIO10, Raspberry_PI_GDIO_External_Board.GPIO_10
  N9: Raspberry_Pi_3_Model_B+.GPIO9, Raspberry_PI_GDIO_External_Board.GPIO_9
  N10: Raspberry_Pi_3_Model_B+.GPIO11, Raspberry_PI_GDIO_External_Board.GPIO_11
  N11: Raspberry_Pi_3_Model_B+.ID_SD, Raspberry_PI_GDIO_External_Board.ID_SD
  N12: Raspberry_Pi_3_Model_B+.GPIO5, Raspberry_PI_GDIO_External_Board.GPIO_5
  N13: Raspberry_Pi_3_Model_B+.GPIO6, Raspberry_PI_GDIO_External_Board.GPIO_6
  N14: Raspberry_Pi_3_Model_B+.GPIO13, Raspberry_PI_GDIO_External_Board.GPIO_13
  N15: Raspberry_Pi_3_Model_B+.GPIO19, Raspberry_PI_GDIO_External_Board.GPIO_19
  N16: Raspberry_Pi_3_Model_B+.GPIO26, Raspberry_PI_GDIO_External_Board.GPIO_26
  N17: Raspberry_Pi_3_Model_B+.GPIO21, Raspberry_PI_GDIO_External_Board.GPIO_21
  N18: Raspberry_Pi_3_Model_B+.GPIO20, Raspberry_PI_GDIO_External_Board.GPIO_20
  N19: Raspberry_Pi_3_Model_B+.GPIO16, Raspberry_PI_GDIO_External_Board.GPIO_16
  N20: Raspberry_Pi_3_Model_B+.GPIO12, Raspberry_PI_GDIO_External_Board.GPIO_12
  N21: Raspberry_Pi_3_Model_B+.ID_SC, Raspberry_PI_GDIO_External_Board.ID_SC
  N22: Raspberry_Pi_3_Model_B+.GPIO7, Raspberry_PI_GDIO_External_Board.GPIO_7
  N23: Raspberry_Pi_3_Model_B+.GPIO8, Raspberry_PI_GDIO_External_Board.GPIO_8
  N24: Raspberry_Pi_3_Model_B+.GPIO25, Raspberry_PI_GDIO_External_Board.GPIO_25
  N25: Raspberry_Pi_3_Model_B+.GPIO24, Raspberry_PI_GDIO_External_Board.GPIO_24
  N26: Raspberry_Pi_3_Model_B+.GPIO23, Raspberry_PI_GDIO_External_Board.GPIO_23
  N27: Raspberry_Pi_3_Model_B+.GPIO18, Raspberry_PI_GDIO_External_Board.GPIO_18
  N28: Raspberry_Pi_3_Model_B+.GPIO15, Raspberry_PI_GDIO_External_Board.GPIO_15
  N29: Raspberry_Pi_3_Model_B+.GPIO14, Raspberry_PI_GDIO_External_Board.GPIO_14
  5V: Raspberry_Pi_3_Model_B+.5V, Raspberry_PI_GDIO_External_Board.5V
  N30: Raspberry_PI_GDIO_External_Board.SDA, LCM1602_IIC2.SDA
  N31: Raspberry_PI_GDIO_External_Board.5.0V#3, BUTTON_ORANGE.Pin_3, BUTTON_ORANGE.Pin_4, BUTTON_YELLOW.Pin_3, BUTTON_YELLOW.Pin_4, BUTTON_GREEN.Pin_3, BUTTON_GREEN.Pin_4, LCM1602_IIC2.VCC
  N32: Raspberry_PI_GDIO_External_Board.SCL, LCM1602_IIC2.SCL
  N33: Raspberry_PI_GDIO_External_Board.GND#5, LED_ORANGE.cathode, LED_GREEN.cathode, LED_YELLOW.cathode, LED_BLUE.cathode, R5.Pin_0, R6.Pin_0, R7.Pin_0, PIEZO.pin1, LCM1602_IIC2.GND
  N34: Raspberry_PI_GDIO_External_Board.#17, LED_ORANGE.anode, R1.Pin_0, R1.Pin_1
  N35: Raspberry_PI_GDIO_External_Board.#18, LED_BLUE.anode, R4.Pin_0, R4.Pin_1
  N36: Raspberry_PI_GDIO_External_Board.#27, LED_GREEN.anode, R2.Pin_0, R2.Pin_1
  N37: Raspberry_PI_GDIO_External_Board.#22, LED_YELLOW.anode, R3.Pin_0, R3.Pin_1
  N38: Raspberry_PI_GDIO_External_Board.#23, BUTTON_ORANGE.Pin_1, BUTTON_ORANGE.Pin_2, R5.Pin_1
  N39: Raspberry_PI_GDIO_External_Board.#24, BUTTON_GREEN.Pin_1, BUTTON_GREEN.Pin_2, R7.Pin_1
  N40: Raspberry_PI_GDIO_External_Board.#25, BUTTON_YELLOW.Pin_1, BUTTON_YELLOW.Pin_2, R6.Pin_1
  N41: Raspberry_PI_GDIO_External_Board.#16, PIEZO.pin2
  VSS: LCD2.VSS, LCM1602_IIC2.VSS
  VDD: LCD2.VDD, LCM1602_IIC2.VDD
  N42: LCD2.V0, LCM1602_IIC2.V0
  N43: LCD2.RS, LCM1602_IIC2.RS
  N44: LCD2.R/W, LCM1602_IIC2.RW
  N45: LCD2.E, LCM1602_IIC2.E
  N46: LCD2.DB0, LCM1602_IIC2.D0
  N47: LCD2.DB1, LCM1602_IIC2.D1
  N48: LCD2.DB2, LCM1602_IIC2.D2
  N49: LCD2.DB3, LCM1602_IIC2.D3
  N50: LCD2.DB4, LCM1602_IIC2.D4
  N51: LCD2.DB5, LCM1602_IIC2.D5
  N52: LCD2.DB6, LCM1602_IIC2.D6
  N53: LCD2.DB7, LCM1602_IIC2.D7
  N54: LCD2.LED+, LCM1602_IIC2.A
  N55: LCD2.LED-, LCM1602_IIC2.K
  N56: LCM1602_IIC2.LED_A, LCM1602_IIC2.LED_B

custom parts:
  T Cobbler Plus: The T-Cobbler Plus is an add on prototyping board from Adafruit specifically designed for the Raspberry Pi B+ that can break out all those tasty power, GPIO, I2C and SPI pins from the 40-pin header onto a solderless breadboard. This set will make "cobbling together" prototypes with the Pi super easy. The T-Cobbler Plus can plug into any solderless breadboard.
  LCM1602 IIC: I2C-Module to use a 1602 or 2004 LCD on with the wire.h libory Serial LCD Modul
